// Logisim project trabalhoFinal1.circ as structural Verilog: 14 circuits, main circuit Seletor
module main (
  input  [2:0] sel,
  input  [3:0] A,
  input  [3:0] B,
  output [4:0] S
);

  menu_logico menu_logico_1 (.sel(sel), .A(A), .B(B), .S(S));
endmodule

module menu_logico (
  input  [2:0] sel,
  input  [3:0] A,
  input  [3:0] B,
  output [4:0] S
);

  wire seletor_1_s1, seletor_1_s2, seletor_1_s3, seletor_1_s4, seletor_1_s5, seletor_1_s6, seletor_1_s7,
       seletor_1_s8;
  wire [4:0] adder_4bits_000_1_out_4, and_vet_011_1_s, gerador_de_paridade_111_1_s, mascara_ligar_101_1_s,
       mascara_modificar_110_1_s, or_vet_100_1_s, subtractor_4bits_001_1_out_4,
       twocomplementsub_4bits_010_1_out_4;

  Seletor seletor_1 (
    .A(sel), .s1(seletor_1_s1), .s2(seletor_1_s2), .s3(seletor_1_s3), .s4(seletor_1_s4), .s5(seletor_1_s5),
    .s6(seletor_1_s6), .s7(seletor_1_s7), .s8(seletor_1_s8));
  adder_4bits_000 adder_4bits_000_1 (.sig(seletor_1_s1), .A(A), .B(B), .out_4(adder_4bits_000_1_out_4));
  subtractor_4bits_001 subtractor_4bits_001_1 (.sig(seletor_1_s2), .A(A), .B(B), .out_4(subtractor_4bits_001_1_out_4));
  twocomplementsub_4bits_010 twocomplementsub_4bits_010_1 (
    .sig(seletor_1_s3), .A(A), .B(B), .out_4(twocomplementsub_4bits_010_1_out_4));
  and_vet_011 and_vet_011_1 (.sig(seletor_1_s4), .A(A), .B(B), .S(and_vet_011_1_s));
  or_vet_100 or_vet_100_1 (.sig(seletor_1_s5), .A(A), .B(B), .S(or_vet_100_1_s));
  mascara_ligar_101 mascara_ligar_101_1 (.sig(seletor_1_s6), .A(A), .B(B), .S(mascara_ligar_101_1_s));
  mascara_modificar_110 mascara_modificar_110_1 (.sig(seletor_1_s7), .A(A), .B(B), .S(mascara_modificar_110_1_s));
  gerador_de_paridade_111 gerador_de_paridade_111_1 (.sig(seletor_1_s8), .A(A), .B(B), .S(gerador_de_paridade_111_1_s));
  super_or super_or_1 (
    .in_1(adder_4bits_000_1_out_4), .in_2(subtractor_4bits_001_1_out_4),
    .in_3(twocomplementsub_4bits_010_1_out_4), .in_4(and_vet_011_1_s), .in_5(or_vet_100_1_s),
    .in_6(mascara_ligar_101_1_s), .in_7(mascara_modificar_110_1_s), .in_8(gerador_de_paridade_111_1_s),
    .out_9(S));

  // Notes on the sheet:
  //   Menu de Operações Lógicas
  //   Seletor
  //   Operações Lógicas
  //   Filtro de Saídas
endmodule

module Seletor (
  input  [2:0] A,
  output s1,
  output s2,
  output s3,
  output s4,
  output s5,
  output s6,
  output s7,
  output s8
);

  wire not_1_out, not_2_out, not_3_out;

  not not_1 (not_1_out, A[2]);
  not not_2 (not_2_out, A[1]);
  not not_3 (not_3_out, A[0]);
  and and_1 (s1, not_1_out, not_2_out, not_3_out);
  and and_2 (s2, not_1_out, not_2_out, A[0]);
  and and_3 (s3, not_1_out, A[1], not_3_out);
  and and_4 (s4, not_1_out, A[1], A[0]);
  and and_5 (s5, A[2], not_2_out, not_3_out);
  and and_6 (s6, A[2], not_2_out, A[0]);
  and and_7 (s7, A[2], A[1], not_3_out);
  and and_8 (s8, A[2], A[1], A[0]);
endmodule

module adder_4bits_000 (
  input  sig,
  input  [3:0] A,
  input  [3:0] B,
  output [4:0] out_4
);

  wire A0_out, A1_out, A2_out, A3_out, B0_out, B1_out, B2_out, B3_out, full_adder_2_cout, full_adder_3_cout,
       full_adder_4_cout;

  and B3 (B3_out, A[3], sig);
  and B2 (B2_out, A[2], sig);
  full_adder full_adder_1 (.A(B3_out), .B(A3_out), .Cin(full_adder_2_cout), .S(out_4[3]), .Cout(out_4[4]));
  and B1 (B1_out, A[1], sig);
  and B0 (B0_out, A[0], sig);
  full_adder full_adder_2 (.A(B2_out), .B(A2_out), .Cin(full_adder_3_cout), .S(out_4[2]), .Cout(full_adder_2_cout));
  and A3 (A3_out, B[3], sig);
  and A2 (A2_out, B[2], sig);
  full_adder full_adder_3 (.A(B1_out), .B(A1_out), .Cin(full_adder_4_cout), .S(out_4[1]), .Cout(full_adder_3_cout));
  and A1 (A1_out, B[1], sig);
  and A0 (A0_out, B[0], sig);
  full_adder full_adder_4 (.A(B0_out), .B(A0_out), .Cin(1'b0), .S(out_4[0]), .Cout(full_adder_4_cout));
endmodule

module subtractor_4bits_001 (
  input  sig,
  input  [3:0] A,
  input  [3:0] B,
  output [4:0] out_4
);

  wire A0_out, A1_out, A2_out, A3_out, B0_out, B1_out, B2_out, B3_out, full_subtractor_2_cout,
       full_subtractor_3_cout, full_subtractor_4_cout;

  and B3 (B3_out, A[3], sig);
  and B2 (B2_out, A[2], sig);
  full_subtractor full_subtractor_1 (
    .A(B3_out), .B(A3_out), .Cin(full_subtractor_2_cout), .S(out_4[3]), .Cout(out_4[4]));
  and B1 (B1_out, A[1], sig);
  and B0 (B0_out, A[0], sig);
  full_subtractor full_subtractor_2 (
    .A(B2_out), .B(A2_out), .Cin(full_subtractor_3_cout), .S(out_4[2]), .Cout(full_subtractor_2_cout));
  and A3 (A3_out, B[3], sig);
  and A2 (A2_out, B[2], sig);
  full_subtractor full_subtractor_3 (
    .A(B1_out), .B(A1_out), .Cin(full_subtractor_4_cout), .S(out_4[1]), .Cout(full_subtractor_3_cout));
  and A1 (A1_out, B[1], sig);
  and A0 (A0_out, B[0], sig);
  full_subtractor full_subtractor_4 (.A(B0_out), .B(A0_out), .Cin(1'b0), .S(out_4[0]), .Cout(full_subtractor_4_cout));
endmodule

module twocomplementsub_4bits_010 (
  input  sig,
  input  [3:0] A,
  input  [3:0] B,
  output [4:0] out_4
);

  wire A0_out, A1_out, A2_out, A3_out, and_1_out, B0_out, B1_out, B2_out, B3_out, full_adder_2_cout,
       full_adder_3_cout, full_adder_4_cout, not_1_out, not_2_out, not_3_out, not_4_out;

  and A3 (A3_out, A[3], sig);
  and A2 (A2_out, A[2], sig);
  full_adder full_adder_1 (.A(A3_out), .B(B3_out), .Cin(full_adder_2_cout), .S(out_4[3]), .Cout(out_4[4]));
  and A1 (A1_out, A[1], sig);
  and A0 (A0_out, A[0], sig);
  full_adder full_adder_2 (.A(A2_out), .B(B2_out), .Cin(full_adder_3_cout), .S(out_4[2]), .Cout(full_adder_2_cout));
  not not_1 (not_1_out, B[3]);
  not not_2 (not_2_out, B[2]);
  and B3 (B3_out, not_1_out, sig);
  and B2 (B2_out, not_2_out, sig);
  full_adder full_adder_3 (.A(A1_out), .B(B1_out), .Cin(full_adder_4_cout), .S(out_4[1]), .Cout(full_adder_3_cout));
  not not_3 (not_3_out, B[1]);
  not not_4 (not_4_out, B[0]);
  and B1 (B1_out, not_3_out, sig);
  and B0 (B0_out, not_4_out, sig);
  and and_1 (and_1_out, sig, 1'b1);
  full_adder full_adder_4 (.A(A0_out), .B(B0_out), .Cin(and_1_out), .S(out_4[0]), .Cout(full_adder_4_cout));
endmodule

module and_vet_011 (
  input  sig,
  input  [3:0] A,
  input  [3:0] B,
  output [4:0] S
);

  wire S0_out, S1_out, S2_out, S3_out;

  and S3 (S3_out, B[3], A[3]);
  and S2 (S2_out, B[2], A[2]);
  and and_1 (S[2], S2_out, sig);
  and and_2 (S[3], S3_out, sig);
  and S1 (S1_out, B[1], A[1]);
  and S0 (S0_out, A[0], B[0]);
  and and_3 (S[0], S0_out, sig);
  and and_4 (S[1], S1_out, sig);

  assign S[4] = 1'b0;
endmodule

module or_vet_100 (
  input  sig,
  input  [3:0] A,
  input  [3:0] B,
  output [4:0] S
);

  wire S0_out, S1_out, S2_out, S3_out;

  or S3 (S3_out, B[3], A[3]);
  or S2 (S2_out, B[2], A[2]);
  and and_1 (S[2], S2_out, sig);
  and and_2 (S[3], S3_out, sig);
  or S1 (S1_out, B[1], A[1]);
  or S0 (S0_out, A[0], B[0]);
  and and_3 (S[0], S0_out, sig);
  and and_4 (S[1], S1_out, sig);

  assign S[4] = 1'b0;
endmodule

module mascara_ligar_101 (
  input  sig,
  input  [3:0] A,
  input  [3:0] B,
  output [4:0] S
);

  wire S0_out, S1_out, S2_out, S3_out;

  or S3 (S3_out, B[3], A[3]);
  or S2 (S2_out, B[2], A[2]);
  and and_1 (S[2], S2_out, sig);
  and and_2 (S[3], S3_out, sig);
  or S1 (S1_out, B[1], A[1]);
  or S0 (S0_out, A[0], B[0]);
  and and_3 (S[0], S0_out, sig);
  and and_4 (S[1], S1_out, sig);

  assign S[4] = 1'b0;
endmodule

module mascara_modificar_110 (
  input  sig,
  input  [3:0] A,
  input  [3:0] B,
  output [4:0] S
);

  wire xor_1_out, xor_2_out, xor_3_out, xor_4_out;

  xor xor_1 (xor_1_out, B[3], A[3]);
  xor xor_2 (xor_2_out, B[2], A[2]);
  and and_1 (S[2], xor_2_out, sig);
  and and_2 (S[3], xor_1_out, sig);
  xor xor_3 (xor_3_out, B[1], A[1]);
  xor xor_4 (xor_4_out, A[0], B[0]);
  and and_3 (S[0], xor_4_out, sig);
  and and_4 (S[1], xor_3_out, sig);

  assign S[4] = 1'b0;
endmodule

module gerador_de_paridade_111 (
  input  sig,
  input  [3:0] A,
  input  [3:0] B,
  output [4:0] S
);

  wire and_1_out, and_2_out, and_3_out, and_4_out, not_1_out, not_2_out, xor_1_out, xor_2_out;

  not not_1 (not_1_out, A[3]);
  and and_1 (and_1_out, not_1_out, sig);
  and and_2 (and_2_out, A[2], sig);
  xor xor_1 (xor_1_out, and_1_out, and_2_out);
  not not_2 (not_2_out, A[1]);
  and and_3 (and_3_out, not_2_out, sig);
  and and_4 (and_4_out, A[0], sig);
  xor xor_2 (xor_2_out, and_3_out, and_4_out);
  xor xor_3 (S[0], xor_1_out, xor_2_out);

  assign B[2:0] = {3{B[3]}};
  assign S[4:1] = 4'b0000;
  // also tied to GND on the sheet: B[3]
endmodule

module full_adder (
  input  A,
  input  B,
  input  Cin,
  output S,
  output Cout
);

  wire and_1_out, and_2_out, and_3_out, xor_1_out;

  xor xor_1 (xor_1_out, A, B);
  and and_1 (and_1_out, A, B);
  and and_2 (and_2_out, A, Cin);
  and and_3 (and_3_out, B, Cin);
  xor xor_2 (S, xor_1_out, Cin);
  or or_1 (Cout, and_1_out, and_2_out, and_3_out);

  // Notes on the sheet:
  //   S = (A ⊕ B) ⊕ Cin
  //   Cout = (A . B) + (A . Cin) + (B . Cin)
endmodule

module full_subtractor (
  input  A,
  input  B,
  input  Cin,
  output S,
  output Cout
);

  wire and_1_out, and_2_out, and_3_out, not_1_out, xor_1_out;

  not not_1 (not_1_out, A);
  xor xor_1 (xor_1_out, A, B);
  and and_1 (and_1_out, not_1_out, B);
  and and_2 (and_2_out, not_1_out, Cin);
  and and_3 (and_3_out, B, Cin);
  xor xor_2 (S, xor_1_out, Cin);
  or or_1 (Cout, and_1_out, and_2_out, and_3_out);

  // Notes on the sheet:
  //   S = (A ⊕ B) ⊕ Cin
  //   Cout = (A' . B) + (A' . Cin) + (B . Cin)
endmodule

module super_or (
  input  [4:0] in_1,
  input  [4:0] in_2,
  input  [4:0] in_3,
  input  [4:0] in_4,
  input  [4:0] in_5,
  input  [4:0] in_6,
  input  [4:0] in_7,
  input  [4:0] in_8,
  output [4:0] out_9
);

  wire A0_out, E0_out, F0_out, or_1_out, or_2_out, or_3_out, or_4_out, or_5_out, or_6_out, or_7_out,
       or_8_out, or_9_out, or_10_out, or_11_out, or_12_out, or_13_out, or_18_out, or_19_out, or_20_out,
       or_21_out, or_22_out, or_23_out, or_24_out, or_25_out, or_26_out, or_27_out, or_28_out, or_29_out,
       or_30_out, or_31_out;

  or or_1 (or_1_out, in_2[4], in_1[4]);
  or or_2 (or_2_out, in_2[3], in_1[3]);
  or or_3 (or_3_out, in_2[2], in_1[2]);
  or or_4 (or_4_out, in_2[1], in_1[1]);
  or A0 (A0_out, in_2[0], in_1[0]);
  or or_5 (or_5_out, or_9_out, or_1_out);
  or or_6 (or_6_out, or_10_out, or_2_out);
  or or_7 (or_7_out, or_11_out, or_3_out);
  or or_8 (or_8_out, or_12_out, or_4_out);
  or E0 (E0_out, or_13_out, A0_out);
  or or_9 (or_9_out, in_4[4], in_3[4]);
  or or_10 (or_10_out, in_4[3], in_3[3]);
  or or_11 (or_11_out, in_4[2], in_3[2]);
  or or_12 (or_12_out, in_4[1], in_3[1]);
  or or_13 (or_13_out, in_4[0], in_3[0]);
  or or_14 (out_9[4], or_23_out, or_5_out);
  or or_15 (out_9[3], or_24_out, or_6_out);
  or or_16 (out_9[2], or_25_out, or_7_out);
  or or_17 (out_9[1], or_26_out, or_8_out);
  or or_18 (or_18_out, in_6[4], in_5[4]);
  or or_19 (or_19_out, in_6[3], in_5[3]);
  or G0 (out_9[0], F0_out, E0_out);
  or or_20 (or_20_out, in_6[2], in_5[2]);
  or or_21 (or_21_out, in_6[1], in_5[1]);
  or or_22 (or_22_out, in_6[0], in_5[0]);
  or or_23 (or_23_out, or_27_out, or_18_out);
  or or_24 (or_24_out, or_28_out, or_19_out);
  or or_25 (or_25_out, or_29_out, or_20_out);
  or or_26 (or_26_out, or_30_out, or_21_out);
  or F0 (F0_out, or_31_out, or_22_out);
  or or_27 (or_27_out, in_8[4], in_7[4]);
  or or_28 (or_28_out, in_8[3], in_7[3]);
  or or_29 (or_29_out, in_8[2], in_7[2]);
  or or_30 (or_30_out, in_8[1], in_7[1]);
  or or_31 (or_31_out, in_8[0], in_7[0]);
endmodule
